# Fritzing sketch sag_ino version 1 (saved by Fritzing 0.8.7b)
breadboards: 1

parts:
  Parte1 = Arduino Mega 2560 (Rev3)
  RGB1 = RGB LED - (4 legs) [package="5 mm [THT]"]
  hygrometer1 = Humidity and Temperature Sensor RHT03

nets:
  N1: Parte1.A0, hygrometer1.Data-signal
  N2: Parte1.D3_PWM, RGB1.red_cathode
  N3: Parte1.D6_PWM, RGB1.blue_cathode
  N4: RGB1.green_cathode, hygrometer1.GND_1
